// Logisim project 4bitALU.circ as structural Verilog: 1 circuit, main circuit main
module main (
  input  [3:0] A,
  input  [3:0] B,
  input  [2:0] s2s1s0,
  output Z,
  output S,
  output V,
  output C,
  output S4,
  output S3,
  output S2,
  output S1
);

  wire n7404_1_p11, n7404_1_p13, n7408_1_p1, n7408_1_p2, n7408_1_p12, n7408_3_p10, n7432_1_p1, n7432_1_p3,
       n7432_1_p6, n7432_1_p9, n7432_1_p11, n7432_2_p3, n7432_2_p6, n7432_2_p14, n7483_1_p2, n7483_1_p4,
       n7483_1_p6, n7483_1_p9, n7483_1_p11, n7483_1_p12, n7483_1_p14, n7483_1_p15, n7483_2_p1, n7483_2_p3,
       n7483_2_p5, n7483_2_p8, n7483_2_p11, n7483_2_p13, n7483_2_p14, n7486_1_p3, n7486_1_p6, n7486_1_p11,
       n7486_1_p14;

  // _7432 7432_1: pin names not known; wires that end beside it: n7432_1_p1, S3, n7432_1_p3, n7432_1_p3, S, n7432_1_p6, 1'b0, 1'b1, n7432_1_p9, B[3], n7432_1_p11, S1, S2, n7432_1_p1
  // _7483 7483_1: pin names not known; wires that end beside it: 1'b0, n7483_1_p2, 1'b1, n7483_1_p4, 1'b1, n7483_1_p6, 1'b0, 1'b0, n7483_1_p9, S, n7483_1_p11, n7483_1_p12, 1'b0, n7483_1_p14, n7483_1_p15, S3
  // _7408 7408_1: pin names not known; wires that end beside it: n7408_1_p1, n7408_1_p2, n7483_1_p12, n7432_1_p11, A[3], n7483_1_p2, 1'b0, 1'b1, n7483_1_p6, n7408_1_p2, n7483_1_p4, n7408_1_p12, s2s1s0[0], n7483_1_p9
  // _7483 7483_2: pin names not known; wires that end beside it: n7483_2_p1, 1'b1, n7483_2_p3, 1'b1, n7483_2_p5, 1'b0, 1'b0, n7483_2_p8, S2, n7408_1_p1, n7483_2_p11, 1'b0, n7483_2_p13, n7483_2_p14, S1, B[2]
  // _7432 7432_2: pin names not known; wires that end beside it: B[1], n7432_1_p9, n7432_2_p3, n7432_1_p9, B[2], n7432_2_p6, 1'b0, 1'b1, s2s1s0[0], n7408_1_p2, n7432_1_p9, n7432_1_p9, B[0], n7432_2_p14
  // _7408 7408_2: pin names not known; wires that end beside it: n7483_1_p11, n7408_1_p2, C, 1'b1
  // _7408 7408_3: pin names not known; wires that end beside it: n7432_2_p14, A[0], n7483_2_p14, n7432_2_p3, A[1], n7483_2_p1, 1'b0, 1'b0, 1'b1, n7408_3_p10, s2s1s0[0], n7483_2_p13, n7408_1_p2, s2s1s0[1], n7483_2_p11
  // _7486 7486_1: pin names not known; wires that end beside it: s2s1s0[2], B[2], n7486_1_p3, s2s1s0[2], B[3], n7486_1_p6, 1'b0, 1'b1, s2s1s0[2], B[0], n7486_1_p11, s2s1s0[2], B[1], n7486_1_p14, 1'b0
  // _7404 7404_1: pin names not known; wires that end beside it: n7486_1_p11, n7408_3_p10, n7486_1_p6, n7408_1_p12, n7432_1_p6, Z, 1'b1, s2s1s0[2], n7408_1_p2, n7486_1_p14, n7404_1_p11, n7486_1_p3, n7404_1_p13
  // _7486 7486_2: pin names not known; wires that end beside it: C, n7483_1_p4, V, 1'b0, 1'b1
  // _7408 7408_4: pin names not known; wires that end beside it: n7404_1_p11, s2s1s0[0], n7483_2_p8, n7404_1_p13, s2s1s0[0], n7483_1_p14, 1'b0, 1'b1, n7408_1_p2, n7483_2_p5, n7483_2_p3, n7432_2_p6, A[2], n7483_1_p15

  assign S4 = S;
endmodule
