// Logisim project 4bitMIPS.circ as structural Verilog: 6 circuits, main circuit RegisterFile
module RegisterFile (
  input  RegWrite,
  input  [3:0] ReadRegister1,
  input  [3:0] ReadRegister2,
  input  [3:0] WriteRegister,
  input  [3:0] WriteData,
  input  Clear,
  input  Clock,
  output [3:0] ReadData1,
  output [3:0] ReadData2
);

  wire decoder_1_out0, decoder_1_out1, decoder_1_out2, decoder_1_out3, decoder_1_out4, decoder_1_out5,
       decoder_1_out7, n7408_1_p3, n7408_1_p6, n7408_1_p9, n7408_1_p12, n7408_2_p3, n7408_2_p6, n7408_2_p9;
  wire [3:0] sp_q, t0_q, t1_q, t2_q, t3_q, t4_q, zero_q;

  Decoder #(.select(3)) decoder_1 (
    .out0(decoder_1_out0), .out1(decoder_1_out1), .out2(decoder_1_out2), .out3(decoder_1_out3),
    .out4(decoder_1_out4), .out5(decoder_1_out5), .out7(decoder_1_out7), .sel(WriteRegister[2:0]));  // open: out6, en
  Register #(.width(4)) t0 (.D(WriteData), .en(n7408_1_p3), .Q(t0_q), .clk(Clock), .clr(Clear));
  Register #(.width(4)) t1 (.D(WriteData), .en(n7408_1_p6), .Q(t1_q), .clk(Clock), .clr(Clear));
  Register #(.width(4)) t2 (.D(WriteData), .en(n7408_1_p9), .Q(t2_q), .clk(Clock), .clr(Clear));
  Register #(.width(4)) t3 (.D(WriteData), .en(n7408_1_p12), .Q(t3_q), .clk(Clock), .clr(Clear));
  Register #(.width(4)) t4 (.D(WriteData), .en(n7408_2_p3), .Q(t4_q), .clk(Clock), .clr(Clear));
  Register #(.width(4)) zero (.D(4'b0000), .en(n7408_2_p6), .Q(zero_q), .clk(Clock), .clr(Clear));
  // _7408 7408_1: pin names not known; wires that end beside it: decoder_1_out0, RegWrite, n7408_1_p3, decoder_1_out1, RegWrite, n7408_1_p6, decoder_1_out2, RegWrite, n7408_1_p9, decoder_1_out3, RegWrite, n7408_1_p12
  // _7408 7408_2: pin names not known; wires that end beside it: decoder_1_out4, RegWrite, n7408_2_p3, decoder_1_out7, RegWrite, n7408_2_p6, decoder_1_out5, RegWrite, n7408_2_p9
  Multiplexer #(.select(3), .width(4)) multiplexer_1 (
    .in0(t0_q), .in1(t1_q), .in2(t2_q), .in3(t3_q), .in4(t4_q), .in5(sp_q), .in7(zero_q), .out(ReadData1),
    .sel(ReadRegister1[2:0]));  // open: in6, en
  Register #(.width(4)) sp (.D(WriteData), .en(n7408_2_p9), .Q(sp_q), .clk(Clock), .clr(Clear));
  Multiplexer #(.select(3), .width(4)) multiplexer_2 (
    .in0(t0_q), .in1(t1_q), .in2(t2_q), .in3(t3_q), .in4(t4_q), .in5(sp_q), .in7(zero_q), .out(ReadData2),
    .sel(ReadRegister2[2:0]));  // open: in6, en
endmodule

module DataMemory (
  input  [7:0] Address,
  input  [3:0] Write_Data,
  input  Clock,
  input  MemWrite,
  input  MemRead,
  input  Clr,
  output [3:0] Read_Data
);

  RAM #(.dataWidth(4), .bus("separate")) ram_1 (
    .addr(Address), .din(Write_Data), .data(Read_Data), .str(MemWrite), .clk(Clock), .ld(MemRead), .clr(Clr));  // open: sel
endmodule

module Instruction_Memory (
  input  [7:0] Address,
  output [15:0] Output
);

  ROM #(.dataWidth(16)) rom_1 (.addr(Address), .data(Output));  // open: sel

  // Notes on the sheet:
  //   contents of rom_1 (hex, n*v repeats v):
  //   bf93 7fae 19a8 29ab d8ac 5a93 aaa1 4ab1 61c0 fbb1 8aa4 5d90 bddf 5da0 bddf 6190 8a8 eca1 c995 bdd1
  //   8da0 9ac9 bdd1 8d90 61c0 48a1 6100
endmodule

module Control (
  input  [3:0] Opcode,
  output RegDst,
  output Branch,
  output MemRead,
  output MemToReg,
  output [2:0] ALUOp,
  output MemWrite,
  output ALUSrc,
  output RegWrite,
  output beq,
  output jump
);

  ROM #(.addrWidth(4), .dataWidth(12)) rom_1 (
    .addr(Opcode), .data({jump, beq, RegWrite, ALUSrc, MemWrite, ALUOp, MemToReg, MemRead, Branch, RegDst}));  // open: sel

  // Notes on the sheet:
  //   contents of rom_1 (hex, n*v repeats v):
  //   231 201 211 12 412 180 800 310 30c 221 360 300 330 241 220 250
  //   ALU Operations
  //   000 -> add
  //   001 -> sub
  //   010 -> and
  //   011 -> or
  //   100 -> nor
  //   101 -> sll
  //   110 -> srl
endmodule

module main (
  input  in_1,
  output [3:0] out_2,
  output [3:0] out_3,
  output [7:0] out_4,
  output [7:0] out_5,
  output [15:0] out_6,
  output [3:0] Result
);

  wire alu_1_p5, clock_1_out, control_1_alusrc, control_1_beq, control_1_branch, control_1_jump,
       control_1_memread, control_1_memtoreg, control_1_memwrite, control_1_regdst, control_1_regwrite,
       n7404_1_p2, n7408_1_p3, n7486_1_p3;
  wire [2:0] control_1_aluop;
  wire [3:0] datamemory_1_read_data, multiplexer_1_out, multiplexer_4_out, registerfile_1_readdata2;
  wire [7:0] adder_1_out, adder_2_out_3, multiplexer_3_out, multiplexer_5_out;

  Register register_1 (.D(multiplexer_5_out), .Q(out_4), .clk(clock_1_out), .clr(in_1));  // open: en
  Adder adder_1 (.a(out_4), .b(8'h1), .out(adder_1_out));  // open: cin, cout
  Instruction_Memory instruction_memory_1 (.Address(out_4), .Output(out_6));
  Clock clock_1 (.out(clock_1_out));
  Multiplexer #(.width(4)) multiplexer_1 (
    .in0(out_6[7:4]), .in1(out_6[3:0]), .out(multiplexer_1_out), .sel(control_1_regdst));  // open: en
  Control control_1 (
    .Opcode(out_6[15:12]), .RegDst(control_1_regdst), .Branch(control_1_branch), .MemRead(control_1_memread),
    .MemToReg(control_1_memtoreg), .ALUOp(control_1_aluop), .MemWrite(control_1_memwrite),
    .ALUSrc(control_1_alusrc), .RegWrite(control_1_regwrite), .beq(control_1_beq), .jump(control_1_jump));
  RegisterFile registerfile_1 (
    .RegWrite(control_1_regwrite), .ReadRegister1(out_6[11:8]), .ReadRegister2(out_6[7:4]),
    .WriteRegister(multiplexer_1_out), .WriteData(multiplexer_4_out), .Clear(in_1), .Clock(clock_1_out),
    .ReadData1(out_2), .ReadData2(registerfile_1_readdata2));
  Multiplexer #(.width(4)) multiplexer_2 (
    .in0(registerfile_1_readdata2), .in1(out_6[3:0]), .out(out_3), .sel(control_1_alusrc));  // open: en
  adder adder_2 (.address(out_6[3:0]), ._1st_operand(adder_1_out), .out_3(adder_2_out_3));
  // ALU alu_1: pin names not known; wires that end beside it: out_2, out_3, control_1_aluop, Result, alu_1_p5
  assign out_5 = {{4{Result[3]}}, Result};  // Bit_Extender bit_extender_1
  DataMemory datamemory_1 (
    .Address(out_5), .Write_Data(registerfile_1_readdata2), .Clock(clock_1_out),
    .MemWrite(control_1_memwrite), .MemRead(control_1_memread), .Clr(in_1), .Read_Data(datamemory_1_read_data));
  Multiplexer #(.width(8)) multiplexer_3 (
    .in0(adder_1_out), .in1(adder_2_out_3), .out(multiplexer_3_out), .sel(n7408_1_p3));  // open: en
  // _7486 7486_1: pin names not known; wires that end beside it: control_1_beq, alu_1_p5, n7486_1_p3
  Multiplexer #(.width(4)) multiplexer_4 (
    .in0(Result), .in1(datamemory_1_read_data), .out(multiplexer_4_out), .sel(control_1_memtoreg));  // open: en
  Multiplexer #(.width(8)) multiplexer_5 (
    .in0(multiplexer_3_out), .in1(out_6[11:4]), .out(multiplexer_5_out), .sel(control_1_jump));  // open: en
  // _7404 7404_1: pin names not known; wires that end beside it: n7486_1_p3, n7404_1_p2
  // _7408 7408_1: pin names not known; wires that end beside it: n7404_1_p2, control_1_branch, n7408_1_p3
endmodule

module adder (
  input  [3:0] address,
  input  [7:0] _1st_operand,
  output [7:0] out_3
);

  wire [7:0] bit_extender_1_out;

  assign bit_extender_1_out = {{4{address[3]}}, address};  // Bit_Extender bit_extender_1
  Adder adder_1 (.a(bit_extender_1_out), .b(_1st_operand), .out(out_3));  // open: cin, cout
endmodule
