// Logisim project FloatingPointAdd.circ as structural Verilog: 18 circuits, main circuit main
module main (
  input  [31:0] _1st,
  input  [31:0] _2nd,
  output [31:0] Sum,
  output Overflow,
  output Underflow
);

  FPA fpa_1 (.Underflow(Underflow), .Overflow(Overflow), ._1st(_1st), ._2nd(_2nd), .Sum(Sum));
endmodule

module Significand (
  input  [20:0] Fraction,
  input  Sign,
  output [31:0] Significand
);


  assign Significand = {Sign, 1'b1, Fraction, {9{1'b0}}};
endmodule

module Compare (
  input  [31:0] _1st_Significand,
  input  [9:0] _1st_Exponent,
  input  [31:0] _2nd_Significand,
  input  [9:0] _2nd_Exponent,
  output [9:0] Exponent,
  output [30:0] Smaller_Significand,
  output [31:0] Larger_Significand,
  output Larger_sign
);

  wire subtractor_1_bout, subtractor_2_bout;
  wire [9:0] multiplexer_1_out, negator_1_out, subtractor_1_out;
  wire [30:0] multiplexer_4_out;
  wire [31:0] multiplexer_3_out;

  Subtractor #(.width(10)) subtractor_1 (
    .a(_1st_Exponent), .b(_2nd_Exponent), .out(subtractor_1_out), .bin(1'b0), .bout(subtractor_1_bout));
  Subtractor #(.width(32)) subtractor_2 (
    .a({_1st_Exponent, _1st_Significand[30:9]}), .b({_2nd_Exponent, _2nd_Significand[30:9]}),
    .bout(subtractor_2_bout));  // open: out, bin
  Negator #(.width(10)) negator_1 (.in(subtractor_1_out), .out(negator_1_out));
  Multiplexer #(.width(10)) multiplexer_1 (
    .in0(subtractor_1_out), .in1(negator_1_out), .out(multiplexer_1_out), .sel(subtractor_1_bout));  // open: en
  Multiplexer #(.width(10)) multiplexer_2 (
    .in0(_1st_Exponent), .in1(_2nd_Exponent), .out(Exponent), .sel(subtractor_1_bout));  // open: en
  Multiplexer #(.width(32)) multiplexer_3 (
    .in0(_2nd_Significand), .in1(_1st_Significand), .out(multiplexer_3_out), .sel(subtractor_2_bout));  // open: en
  Multiplexer #(.width(32)) multiplexer_4 (
    .in0(_1st_Significand), .in1(_2nd_Significand), .out({Larger_sign, multiplexer_4_out}),
    .sel(subtractor_2_bout));  // open: en
  _10_bit_Shift u_10_bit_shift_1 (
    .Significand_in(multiplexer_3_out[30:0]), .Shift(multiplexer_1_out), .Significand_out(Smaller_Significand));
  assign Larger_Significand = {{1{1'b0}}, multiplexer_4_out};  // Bit_Extender bit_extender_1
endmodule

module Sign_Check (
  input  _1st_sign,
  input  _2nd_sign,
  output Sign_similarity
);

  // _7486 7486_1: pin names not known; wires that end beside it: _1st_sign, _1st_sign, _2nd_sign, Sign_similarity
endmodule

module Inverter (
  input  [30:0] Significand,
  input  Sign,
  output [31:0] Inverted_significand
);

  wire [31:0] bit_extender_1_out, negator_1_out;

  assign bit_extender_1_out = {{1{1'b0}}, Significand};  // Bit_Extender bit_extender_1
  Negator #(.width(32)) negator_1 (.in(bit_extender_1_out), .out(negator_1_out));
  Multiplexer #(.width(32)) multiplexer_1 (
    .in0(bit_extender_1_out), .in1(negator_1_out), .out(Inverted_significand), .sel(Sign));  // open: en
endmodule

module Adder (
  input  [31:0] _1st,
  input  [31:0] _2nd,
  output [31:0] Output
);

  Adder_part #(.width(32)) adder_1 (.a(_1st), .b(_2nd), .out(Output), .cin(1'b0));  // open: cout
endmodule

module FPA (
  input  [31:0] _1st,
  input  [31:0] _2nd,
  output Underflow,
  output Overflow,
  output [31:0] Sum
);

  wire compare_1_larger_sign, sign_check_1_sign_similarity;
  wire [9:0] compare_1_exponent, normalizer_1_exponent_out;
  wire [30:0] compare_1_smaller_significand;
  wire [31:0] adder_1_output, compare_1_larger_significand, inverter_1_inverted_significand,
       normalizer_1_significand_out, significand_1_significand, significand_2_significand;

  Sign_Check sign_check_1 (._1st_sign(_1st[31]), ._2nd_sign(_2nd[31]), .Sign_similarity(sign_check_1_sign_similarity));
  Significand significand_1 (.Sign(_1st[31]), .Fraction(_1st[20:0]), .Significand(significand_1_significand));
  Compare compare_1 (
    ._1st_Significand(significand_2_significand), ._1st_Exponent(_2nd[30:21]),
    ._2nd_Significand(significand_1_significand), ._2nd_Exponent(_1st[30:21]), .Exponent(compare_1_exponent),
    .Smaller_Significand(compare_1_smaller_significand), .Larger_Significand(compare_1_larger_significand),
    .Larger_sign(compare_1_larger_sign));
  Inverter inverter_1 (
    .Significand(compare_1_smaller_significand), .Sign(sign_check_1_sign_similarity),
    .Inverted_significand(inverter_1_inverted_significand));
  Adder adder_1 (._1st(inverter_1_inverted_significand), ._2nd(compare_1_larger_significand), .Output(adder_1_output));
  Normalizer normalizer_1 (
    .Exponent(compare_1_exponent), .Significand_in(adder_1_output),
    .Significand_Out(normalizer_1_significand_out), .Exponent_Out(normalizer_1_exponent_out),
    .Overflow(Overflow), .Underflow(Underflow));
  Significand significand_2 (.Sign(_2nd[31]), .Fraction(_2nd[20:0]), .Significand(significand_2_significand));
  Rounder rounder_1 (
    .Significand(normalizer_1_significand_out), .Exponent(normalizer_1_exponent_out),
    .Sign(compare_1_larger_sign), .Final_Output(Sum));  // open: Sticky_Bit, Round_Bit, Guard_bit, Truncated, Action_bit, Last_bit, Rounded_Up
endmodule

module Underflow (
  input  [9:0] Exponent,
  input  [1:0] in_2,
  input  Borrow_out,
  output Underflow
);

  wire n7402_1_p1, n7432_1_p2, nor_gate_10_bits_1_nor_output;

  NOR_gate_10_bits nor_gate_10_bits_1 (.Exponent(Exponent), .NOR_output(nor_gate_10_bits_1_nor_output));
  // _7402 7402_1: pin names not known; wires that end beside it: n7402_1_p1, in_2[0], in_2[1]
  // _7432 7432_1: pin names not known; wires that end beside it: nor_gate_10_bits_1_nor_output, n7432_1_p2, Underflow
  // _7408 7408_1: pin names not known; wires that end beside it: n7402_1_p1, Borrow_out, n7432_1_p2
endmodule

module Truncation (
  input  [31:0] Significand,
  input  [9:0] Exponent,
  input  Sign,
  output [31:0] Output
);


  assign Output = {Sign, Exponent, Significand[29:9]};
endmodule

module Normalizer (
  input  [31:0] Significand_in,
  input  [9:0] Exponent,
  output [31:0] Significand_Out,
  output [9:0] Exponent_Out,
  output Overflow,
  output Underflow
);

  wire NOR_gate_nor_output, subtractor_3_bout;
  wire [4:0] bitfinder_1_index, subtractor_1_out, subtractor_2_out;
  wire [9:0] adder_1_out, bit_extender_1_out, multiplexer_1_out, subtractor_3_out;
  wire [31:0] shifter_1_out, shifter_2_out;

  NOR_gate_10_bits NOR_gate (.Exponent(Exponent), .NOR_output(NOR_gate_nor_output));
  Shifter #(.width(32), .shift("lr")) shifter_1 (.in(Significand_in), .\dist (5'b00001), .out(shifter_1_out));
  BitFinder #(.width(32), .\type ("high1")) bitfinder_1 (
    .in(Significand_in), .index(bitfinder_1_index));  // open: found
  Subtractor #(.width(5)) subtractor_1 (
    .a(5'b01111), .b(bitfinder_1_index), .out(subtractor_1_out));  // open: bin, bout
  Subtractor #(.width(5)) subtractor_2 (
    .a(5'b01111), .b(subtractor_1_out), .out(subtractor_2_out), .bin(1'b0));  // open: bout
  Subtractor #(.width(10)) subtractor_3 (
    .a(Exponent), .b(bit_extender_1_out), .out(subtractor_3_out), .bout(subtractor_3_bout));  // open: bin
  Adder_part #(.width(10)) adder_1 (.a(Exponent), .b(10'h1), .out(adder_1_out));  // open: cin, cout
  Shifter #(.width(32)) shifter_2 (.in(Significand_in), .\dist (subtractor_2_out), .out(shifter_2_out));
  assign bit_extender_1_out = {{5{1'b0}}, subtractor_2_out};  // Bit_Extender bit_extender_1
  Multiplexer #(.select(2), .width(10)) multiplexer_1 (
    .in0(subtractor_3_out), .in1(Exponent), .in2(adder_1_out), .in3(adder_1_out), .out(multiplexer_1_out),
    .sel(Significand_in[31:30]));  // open: en
  Underflow underflow_1 (
    .Exponent(multiplexer_1_out), .in_2(Significand_in[31:30]), .Borrow_out(subtractor_3_bout),
    .Underflow(Underflow));
  Multiplexer #(.select(2), .width(32)) multiplexer_2 (
    .in0(shifter_2_out), .in1(Significand_in), .in2(shifter_1_out), .in3(shifter_1_out),
    .out(Significand_Out), .sel(Significand_in[31:30]));  // open: en
  Multiplexer #(.width(10)) multiplexer_3 (
    .in0(multiplexer_1_out), .in1({10{1'b0}}), .out(Exponent_Out), .sel(NOR_gate_nor_output));  // open: en
  AND_gate_11_bits AND_Gate (
    .first__1__of_significand(Significand_in[31]), .I0(multiplexer_1_out[0]), .I1(multiplexer_1_out[1]),
    .I2(multiplexer_1_out[2]), .I3(multiplexer_1_out[3]), .I4(multiplexer_1_out[4]),
    .I5(multiplexer_1_out[5]), .I6(multiplexer_1_out[6]), .I7(multiplexer_1_out[7]),
    .I8(multiplexer_1_out[8]), .I9(multiplexer_1_out[9]), .Output(Overflow));
endmodule

module NOR_gate_10_bits (
  input  [9:0] Exponent,
  output NOR_output
);

  wire n7432_1_p3, n7432_1_p6, n7432_1_p8, n7432_1_p9, n7432_2_p3, n7432_2_p6, n7432_2_p8, n7432_2_p9;

  // _7432 7432_1: pin names not known; wires that end beside it: Exponent[9], Exponent[8], n7432_1_p3, Exponent[7], n7432_1_p3, n7432_1_p6, Exponent[5], n7432_1_p8, n7432_1_p9, Exponent[6], n7432_1_p6, n7432_1_p8
  // _7432 7432_2: pin names not known; wires that end beside it: n7432_1_p9, Exponent[4], n7432_2_p3, n7432_2_p3, Exponent[3], n7432_2_p6, Exponent[1], n7432_2_p8, n7432_2_p9, Exponent[2], n7432_2_p6, n7432_2_p8
  // _7402 7402_1: pin names not known; wires that end beside it: NOR_output, Exponent[0], n7432_2_p9
endmodule

module AND_gate_11_bits (
  input  first__1__of_significand,
  input  I0,
  input  I1,
  input  I2,
  input  I3,
  input  I4,
  input  I5,
  input  I6,
  input  I7,
  input  I8,
  input  I9,
  output Output
);

  wire n7408_1_p3, n7408_1_p6, n7408_1_p8, n7408_1_p9, n7408_2_p3, n7408_2_p6, n7408_2_p8, n7408_2_p9,
       n7408_3_p3;

  // _7408 7408_1: pin names not known; wires that end beside it: I0, I1, n7408_1_p3, n7408_1_p3, I2, n7408_1_p6, I4, n7408_1_p8, n7408_1_p9, I3, n7408_1_p6, n7408_1_p8
  // _7408 7408_2: pin names not known; wires that end beside it: I5, n7408_1_p9, n7408_2_p3, n7408_2_p3, I6, n7408_2_p6, I8, n7408_2_p8, n7408_2_p9, I7, n7408_2_p6, n7408_2_p8
  // _7408 7408_3: pin names not known; wires that end beside it: I9, n7408_2_p9, n7408_3_p3, n7408_3_p3, first__1__of_significand, Output
endmodule

module Rounder (
  input  [31:0] Significand,
  input  [9:0] Exponent,
  input  Sign,
  output Sticky_Bit,
  output Round_Bit,
  output Guard_bit,
  output [31:0] Truncated,
  output [1:0] Action_bit,
  output Last_bit,
  output [31:0] Rounded_Up,
  output [31:0] Final_Output
);

  wire [4:0] bit_extender_1_out;
  wire [9:0] bit_extender_2_out;
  wire [22:0] adder_1_out;
  wire [22:21] shifter_1_out;
  wire [31:0] multiplexer_1_out, undriven;

  assign bit_extender_1_out = {{4{1'b0}}, adder_1_out[22]};  // Bit_Extender bit_extender_1
  assign bit_extender_2_out = {{9{1'b0}}, adder_1_out[22]};  // Bit_Extender bit_extender_2
  Shifter #(.width(23), .shift("lr")) shifter_1 (
    .in(adder_1_out), .\dist (bit_extender_1_out), .out({shifter_1_out, Rounded_Up[20:0]}));
  Adder_part #(.width(22)) adder_1 (
    .a(Significand[30:9]), .b(22'h1), .out(adder_1_out[21:0]), .cout(adder_1_out[22]));  // open: cin
  Adder_part #(.width(10)) adder_2 (.a(Exponent), .b(bit_extender_2_out), .out(Rounded_Up[30:21]));  // open: cin, cout
  Multiplexer #(.width(32), .enable("false")) multiplexer_1 (
    .in0({Sign, Exponent, Significand[29:9]}), .in1({Sign, Rounded_Up[30:0]}), .out(multiplexer_1_out),
    .sel(Significand[9]));
  OR_gate_7_bits or_gate_7_bits_1 (.in_1(Significand[6:0]), .out_2(Sticky_Bit));
  Action_Selector action_selector_1 (
    .G(Significand[8]), .R(Significand[7]), .S(Sticky_Bit), .A1(Action_bit[1]), .A0(Action_bit[0]));
  Multiplexer #(.select(2), .width(32), .enable("false")) multiplexer_2 (
    .in0({Sign, Exponent, Significand[29:9]}), .in1(multiplexer_1_out), .in2({Sign, Rounded_Up[30:0]}),
    .in3(undriven), .out(Final_Output), .sel(Action_bit));

  assign Guard_bit = Significand[8];
  assign Last_bit = Significand[9];
  assign Round_Bit = Significand[7];
  assign Rounded_Up[31] = Sign;
  assign Truncated = {Sign, Exponent, Significand[29:9]};

  // Notes on the sheet:
  //   Adder
  //   round up
  //   not used
endmodule

module OR_gate_7_bits (
  input  [6:0] in_1,
  output out_2
);

  wire n7432_1_p3, n7432_1_p6, n7432_1_p8, n7432_1_p9, n7432_2_p3;

  // _7432 7432_1: pin names not known; wires that end beside it: in_1[0], in_1[1], n7432_1_p3, n7432_1_p3, in_1[2], n7432_1_p6, in_1[4], n7432_1_p8, n7432_1_p9, in_1[3], n7432_1_p6, n7432_1_p8
  // _7432 7432_2: pin names not known; wires that end beside it: in_1[5], n7432_1_p9, n7432_2_p3, n7432_2_p3, in_1[6], out_2
endmodule

module Action_Selector (
  input  G,
  input  R,
  input  S,
  output A1,
  output A0
);

  wire n7404_1_p1, n7404_1_p2, n7408_1_p6, n7432_1_p3;

  // _7404 7404_1: pin names not known; wires that end beside it: n7404_1_p1, n7404_1_p2, R, n7404_1_p1, S, n7404_1_p2
  // _7432 7432_1: pin names not known; wires that end beside it: R, S, n7432_1_p3
  // _7408 7408_1: pin names not known; wires that end beside it: G, n7432_1_p3, A1, G, n7404_1_p1, n7408_1_p6, n7404_1_p2, n7408_1_p6, A0
endmodule

module _10_bit_Shift (
  input  [30:0] Significand_in,
  input  [9:0] Shift,
  output [30:0] Significand_out
);

  wire [4:0] multiplexer_1_out, multiplexer_2_out, multiplexer_3_out, multiplexer_4_out, multiplexer_5_out;
  wire [30:0] n32_shift_1_out, n32_shift_2_out, n32_shift_3_out, n32_shift_5_out, n128_shift_1_out,
       shifter_1_out, shifter_2_out, shifter_3_out, shifter_4_out, shifter_5_out, shifter_6_out;

  Shifter #(.width(31), .shift("lr")) shifter_1 (.in(Significand_in), .\dist (multiplexer_1_out), .out(shifter_1_out));
  Multiplexer #(.width(5)) multiplexer_1 (
    .in0({5{1'b0}}), .in1(5'b00001), .out(multiplexer_1_out), .sel(Shift[0]));  // open: en
  Multiplexer #(.width(5)) multiplexer_2 (
    .in0({5{1'b0}}), .in1(5'b00010), .out(multiplexer_2_out), .sel(Shift[1]));  // open: en
  Shifter #(.width(31), .shift("lr")) shifter_2 (.in(shifter_1_out), .\dist (multiplexer_2_out), .out(shifter_2_out));
  Multiplexer #(.width(5)) multiplexer_3 (
    .in0({5{1'b0}}), .in1(5'b00100), .out(multiplexer_3_out), .sel(Shift[2]));  // open: en
  Shifter #(.width(31), .shift("lr")) shifter_3 (.in(shifter_2_out), .\dist (multiplexer_3_out), .out(shifter_3_out));
  Multiplexer #(.width(5)) multiplexer_4 (
    .in0({5{1'b0}}), .in1(5'b01000), .out(multiplexer_4_out), .sel(Shift[3]));  // open: en
  Shifter #(.width(31), .shift("lr")) shifter_4 (.in(shifter_5_out), .\dist (multiplexer_5_out), .out(shifter_4_out));
  Shifter #(.width(31), .shift("lr")) shifter_5 (.in(shifter_3_out), .\dist (multiplexer_4_out), .out(shifter_5_out));
  _32_shift u_32_shift_1 (.\input (Shift[5]), .significand(shifter_6_out), .out(n32_shift_1_out));
  Multiplexer #(.width(5)) multiplexer_5 (
    .in0({5{1'b0}}), .in1(5'b01000), .out(multiplexer_5_out), .sel(Shift[4]));  // open: en
  _32_shift u_32_shift_2 (.\input (Shift[6]), .significand(n32_shift_3_out), .out(n32_shift_2_out));
  _32_shift u_32_shift_3 (.\input (Shift[6]), .significand(n32_shift_1_out), .out(n32_shift_3_out));
  Shifter #(.width(31), .shift("lr")) shifter_6 (.in(shifter_4_out), .\dist (multiplexer_5_out), .out(shifter_6_out));
  _128_shift u_128_shift_1 (.\input (Shift[7]), .significand(n32_shift_2_out), .out(n128_shift_1_out));
  _32_shift u_32_shift_4 (.\input (Shift[9]), .significand(n32_shift_5_out), .out(Significand_out));
  _32_shift u_32_shift_5 (.\input (Shift[8]), .significand(n128_shift_1_out), .out(n32_shift_5_out));
endmodule

module _32_shift (
  input  [30:0] significand,
  input  \input ,
  output [30:0] out
);

  wire [4:0] multiplexer_1_out;
  wire [30:0] shifter_1_out, shifter_2_out, shifter_3_out;

  Multiplexer #(.width(5)) multiplexer_1 (
    .in0({5{1'b0}}), .in1(5'b01000), .out(multiplexer_1_out), .sel(\input ));  // open: en
  Shifter #(.width(31), .shift("lr")) shifter_1 (.in(shifter_2_out), .\dist (multiplexer_1_out), .out(shifter_1_out));
  Shifter #(.width(31), .shift("lr")) shifter_2 (.in(significand), .\dist (multiplexer_1_out), .out(shifter_2_out));
  Shifter #(.width(31), .shift("lr")) shifter_3 (.in(shifter_1_out), .\dist (multiplexer_1_out), .out(shifter_3_out));
  Shifter #(.width(31), .shift("lr")) shifter_4 (.in(shifter_3_out), .\dist (multiplexer_1_out), .out(out));
endmodule

module _128_shift (
  input  [30:0] significand,
  input  \input ,
  output [30:0] out
);

  wire [30:0] n32_shift_1_out, n32_shift_3_out, n32_shift_4_out;

  _32_shift u_32_shift_1 (.\input (\input ), .significand(significand), .out(n32_shift_1_out));
  _32_shift u_32_shift_2 (.\input (\input ), .significand(n32_shift_4_out), .out(out));
  _32_shift u_32_shift_3 (.\input (\input ), .significand(n32_shift_1_out), .out(n32_shift_3_out));
  _32_shift u_32_shift_4 (.\input (\input ), .significand(n32_shift_3_out), .out(n32_shift_4_out));
endmodule
